# Fritzing sketch diagrama-circuital (saved by Fritzing 0.9.4)
breadboards: 1

parts:
  Componente1 = Arduino Uno (Rev3)
  IC1 = L293D [package=THT]
  M1 = DC Motor
  Componente2 = HX711 Weighing Sensor Module
  Load_Cell1 = Load Cell - Red/white/black/green

nets:
  N1: Componente1.A0, Componente2.CK/TX
  N2: Componente1.A1, Componente2.DO/RX
  N3: Componente1.D9_PWM, IC1.In_1
  N4: Componente1.D10_PWM/SS, IC1.In_2
  GND: Componente1.GND, IC1.0V, Componente2.GND
  5V: Componente1.5V, IC1.+Vmotor, IC1.+V, Componente2.VCC
  N5: IC1.Out_1_(_Controlled_by_Enable_1_), M1.pin_1
  N6: IC1.Out_2_(_Controlled_by_Enable_1_), M1.pin_2
  N7: Componente2.E+, Load_Cell1.wire1
  N8: Componente2.E-, Load_Cell1.wire3
  N9: Componente2.A+, Load_Cell1.wire4
  N10: Componente2.A-, Load_Cell1.wire2

custom parts:
  Load Cell - Red/white/black/green: A rectangle load cell/weighting pressure Sensor with four wires - Red, white, black, green. Normally corresponding with E+, E-, A+, A- respectively.
